// Logisim project datapath.circ as structural Verilog: 3 circuits, main circuit Datapath
module Datapath (
  input  RegDst,
  input  Branch,
  input  LeMem,
  input  MemparaReg,
  input  ALUOp1,
  input  ALUOp0,
  input  EscreveMem,
  input  OrigALU,
  input  EscreveReg,
  input  Reset,
  input  [3:0] Controle_ALU,
  input  Clear,
  input  Clear_2
);

  wire Clock_out, control_1_escrevemem, control_1_escrevereg, control_1_lemem, control_1_regdst,
       instructiondecode_1_p1, not_1_out, registerfile_1_p1, signextend_1_p4, wordaddress_1_p2,
       wordaddress_2_p1, wordaddress_2_p2;
  wire [1:0] control_1_opalu;
  wire [4:0] instructiondecode_1_p2, instructiondecode_1_p3, multiplexer_1_out;
  wire [31:0] register_1_q;

  Register #(.width(32)) register_1 (.Q(register_1_q), .clk(Clock_out), .clr(Reset));  // open: D, en
  Clock Clock (.out(Clock_out));
  // WordAddress wordaddress_1: pin names not known; wires that end beside it: register_1_q, wordaddress_1_p2, wordaddress_1_p2, 1'b0, 4'b1111
  // InstructionDecode instructiondecode_1: pin names not known; wires that end beside it: instructiondecode_1_p1, instructiondecode_1_p2, instructiondecode_1_p3
  // MIPS_RAM mips_ram_1: pin names not known; wires that end beside it: 1'b0, 1'b1, Clear, instructiondecode_1_p1
  Control control_1 (
    .teste({RegDst, Branch, LeMem, MemparaReg, ALUOp1, ALUOp0, EscreveMem, OrigALU, EscreveReg}),
    .RegDst(control_1_regdst), .LeMem(control_1_lemem), .OpALU(control_1_opalu),
    .EscreveMem(control_1_escrevemem), .EscreveReg(control_1_escrevereg));  // open: op, Branch, MemparaReg, OrigALU
  Multiplexer #(.width(5), .enable("false")) multiplexer_1 (
    .in0(instructiondecode_1_p2), .in1(instructiondecode_1_p3), .out(multiplexer_1_out),
    .sel(control_1_regdst));
  Adder #(.width(32)) adder_1 (.a(32'h4));  // open: b, out, cin, cout
  not not_1 (not_1_out, Clock_out);
  // SignExtend signextend_1: pin names not known; wires that end beside it: not_1_out, control_1_escrevereg, multiplexer_1_out, signextend_1_p4, signextend_1_p4
  // RegisterFile registerfile_1: pin names not known; wires that end beside it: registerfile_1_p1
  // WordAddress wordaddress_2: pin names not known; wires that end beside it: wordaddress_2_p1, wordaddress_2_p2, wordaddress_2_p2, registerfile_1_p1, control_1_escrevemem, 4'b1111
  ALUcontrol alucontrol_1 (.teste(Controle_ALU), .OpALU(control_1_opalu));  // open: funct, Operation
  // BranchAddress branchaddress_1: pin names not known
  // ALU alu_1: pin names not known; wires that end beside it: wordaddress_2_p1
  // MIPS_RAM mips_ram_2: pin names not known; wires that end beside it: not_1_out, control_1_lemem, Clear_2

  // Notes on the sheet:
  //   PC
  //   Opcode
  //   8c0a0000
  //   8c0b0004
  //   014b4820
  //   ac090008
  //   1000ffff
  //   Memória de Instruções
  //   Instruções
  //   Decodificador
  //   main:  lw $t2, 0($zero) 
  //   lw $t3, 4($zero)
  //   add $t1, $t2, $t3
  //   sw $t1, 8($zero)
  //   exit:  beq $zero, $zero, exit
  //   Controle
  //   Controle
  //   lw    001100011
  //   lw    001100011
  //   R     100010001
  //   sw    X00X00110
  //   beq   X10X01000
  //   Registradores
  //   Extensão
  //   Controle ALU
  //   0010 add
  //   0010 add
  //   0010 add
  //   0010 add
  //   0110 sub
  //   ALU
  //   Memória de Dados
  //   Branch
endmodule

module Control (
  input  [8:0] teste,
  input  [5:0] op,
  output RegDst,
  output Branch,
  output LeMem,
  output MemparaReg,
  output [1:0] OpALU,
  output EscreveMem,
  output OrigALU,
  output EscreveReg
);


  assign Branch = teste[7];
  assign EscreveMem = teste[2];
  assign EscreveReg = teste[0];
  assign LeMem = teste[6];
  assign MemparaReg = teste[5];
  assign OpALU = {teste[3], teste[4]};
  assign OrigALU = teste[1];
  assign RegDst = teste[8];
endmodule

module ALUcontrol (
  input  [3:0] teste,
  input  [5:0] funct,
  input  [1:0] OpALU,
  output [3:0] Operation
);


  assign Operation = teste;
endmodule
